// Logisim project Tugas_Tanggal_Lahir_Sederhana.circ as structural Verilog: 1 circuit, main circuit main
module main (
  input  in_1,
  input  TANGGAL,
  input  in_3,
  input  in_4,
  input  in_5,
  input  in_6,
  input  BULAN,
  input  in_8,
  input  in_9
);

  wire A_out, and_1_out, and_2_out, and_3_out, and_4_out, and_5_out, and_6_out, and_7_out, and_8_out,
       and_9_out, and_10_out, and_11_out, and_12_out, and_13_out, and_14_out, and_15_out, and_16_out,
       and_17_out, and_18_out, and_19_out, and_20_out, and_21_out, and_22_out, and_23_out, and_24_out,
       and_25_out, and_26_out, and_27_out, and_28_out, and_29_out, and_30_out, and_31_out, and_32_out,
       and_33_out, and_34_out, and_35_out, and_36_out, and_37_out, and_38_out, and_39_out, and_40_out,
       and_41_out, and_42_out, and_43_out, and_44_out, and_45_out, and_46_out, and_47_out, and_48_out,
       and_49_out, and_50_out, and_51_out, and_52_out, and_53_out, and_54_out, and_55_out, and_56_out,
       and_57_out, and_58_out, and_59_out, and_60_out, and_61_out, and_62_out, and_63_out, and_64_out,
       and_65_out, and_66_out, and_67_out, and_68_out, and_69_out, and_70_out, and_71_out, and_72_out,
       and_73_out, and_74_out, and_75_out, and_76_out, and_77_out, and_78_out, and_79_out, and_80_out,
       and_81_out, and_82_out, and_83_out, and_84_out, and_85_out, and_86_out, and_87_out, and_88_out,
       and_89_out, and_90_out, and_91_out, and_92_out, and_93_out, and_94_out, and_95_out, and_96_out,
       and_97_out, and_98_out, and_99_out, and_100_out, and_101_out, and_102_out, and_103_out, and_104_out,
       and_105_out, and_106_out, and_107_out, and_108_out, and_109_out, and_110_out, and_111_out,
       and_112_out, and_113_out, and_114_out, and_115_out, and_116_out, and_117_out, and_118_out,
       and_119_out, and_120_out, and_121_out, and_122_out, and_123_out, and_124_out, and_125_out,
       and_126_out, and_127_out, and_128_out, and_129_out, and_130_out, and_131_out, and_132_out,
       and_133_out, and_134_out, and_135_out, and_136_out, and_137_out, and_138_out, and_139_out,
       and_140_out, and_141_out, and_142_out, and_143_out, and_144_out, and_145_out, and_146_out,
       and_147_out, and_148_out, and_149_out, and_150_out, and_151_out, and_152_out, and_153_out,
       and_154_out, and_155_out, and_156_out, and_157_out, and_158_out, and_159_out, and_160_out,
       and_161_out, and_162_out, and_163_out, and_164_out, B_out, C_out, D_out, E_out, F_out, G_out, M0_out,
       M1_out, M2_out, M3_out, M4_out, M5_out, M6_out, M7_out, M8_out, M9_out, MS0_out, MS1_out, not_1_out,
       not_2_out, not_3_out, not_4_out, not_5_out, not_6_out, not_7_out, not_8_out, not_9_out, not_10_out,
       not_11_out, not_12_out, not_13_out, not_14_out, not_15_out, not_16_out, not_17_out, not_18_out,
       not_19_out, not_20_out, not_21_out, not_22_out, not_23_out, not_24_out, not_25_out, not_26_out,
       not_27_out, not_28_out, not_29_out, not_30_out, not_31_out, not_32_out, not_33_out, not_34_out,
       not_35_out, not_36_out, not_37_out, not_38_out, not_39_out, not_40_out, not_41_out, not_42_out,
       not_43_out, not_44_out, not_45_out, not_46_out, not_47_out, not_48_out, not_49_out, not_50_out,
       not_51_out, not_52_out, not_53_out, not_54_out, not_55_out, not_56_out, not_57_out, not_58_out,
       not_59_out, not_60_out, not_61_out, not_62_out, not_63_out, not_64_out, not_65_out, not_66_out,
       not_67_out, not_68_out, not_69_out, not_70_out, not_71_out, not_72_out, not_73_out, not_74_out,
       not_75_out, not_76_out, not_77_out, not_78_out, not_79_out, not_80_out, not_81_out, not_82_out,
       not_83_out, not_84_out, not_85_out, not_86_out, not_87_out, not_88_out, not_89_out, not_90_out,
       not_91_out, not_92_out, not_93_out, not_94_out, not_95_out, not_96_out, not_97_out, not_98_out,
       not_99_out, not_100_out, not_101_out, not_102_out, not_103_out, not_104_out, not_105_out, not_106_out,
       not_107_out, not_108_out, or_1_out, or_2_out, or_3_out, or_4_out, or_5_out, or_6_out, or_7_out,
       or_8_out, or_9_out, or_10_out, or_11_out, or_12_out, or_13_out, or_14_out, or_15_out, or_16_out,
       or_17_out, or_18_out, or_19_out, or_20_out, or_21_out, or_22_out, or_23_out, or_24_out, or_25_out,
       or_26_out, or_27_out, or_28_out, or_29_out, or_30_out, or_31_out, or_32_out, or_33_out, or_34_out,
       or_35_out, or_36_out, or_37_out, or_38_out, or_39_out, or_40_out, or_41_out, or_42_out, or_43_out,
       or_44_out, or_45_out, or_46_out, or_47_out, or_48_out, or_49_out, or_50_out, or_51_out, or_52_out,
       or_53_out, or_54_out, or_55_out, or_56_out, or_57_out, or_58_out, or_59_out, or_60_out, or_61_out,
       or_62_out, or_63_out, or_64_out, or_65_out, or_66_out, or_67_out, or_68_out, or_69_out, or_70_out,
       or_71_out, or_72_out, or_73_out, or_74_out, or_75_out, or_76_out, or_77_out, or_78_out, or_79_out,
       or_80_out, or_81_out, or_82_out, or_83_out, or_84_out, or_85_out, or_86_out, or_87_out, or_88_out,
       or_89_out, or_90_out, or_91_out, or_92_out, or_93_out, or_94_out, or_95_out, or_96_out, or_97_out,
       or_98_out, or_99_out, or_100_out, or_101_out, or_102_out, or_103_out, or_104_out, or_105_out,
       or_106_out, or_107_out, or_108_out, or_109_out, or_110_out, or_111_out, or_112_out, or_113_out,
       or_114_out, or_115_out, or_116_out, or_117_out, or_118_out, or_119_out, or_120_out, or_121_out,
       or_122_out, or_123_out, or_124_out, or_125_out, or_126_out, or_127_out, or_128_out, or_129_out,
       or_130_out, P0_out, P1_out, P2_out, P3_out, PA_out, PB_out, PC_out, PD_out, PE_out, PF_out, PG_out;

  not not_1 (not_1_out, in_5);
  not not_2 (not_2_out, in_4);
  not not_3 (not_3_out, in_4);
  not not_4 (not_4_out, in_5);
  not not_5 (not_5_out, in_9);
  and and_1 (and_1_out, not_5_out, not_6_out);
  not not_6 (not_6_out, in_8);
  not not_7 (not_7_out, BULAN);
  and and_2 (and_2_out, in_9, not_8_out);
  not not_8 (not_8_out, in_8);
  not not_9 (not_9_out, BULAN);
  not not_10 (not_10_out, in_9);
  and and_3 (and_3_out, not_10_out, in_8);
  not not_11 (not_11_out, BULAN);
  and and_4 (and_4_out, in_9, in_8);
  not not_12 (not_12_out, BULAN);
  not not_13 (not_13_out, in_9);
  and and_5 (and_5_out, not_13_out, not_14_out);
  not not_14 (not_14_out, in_8);
  and and_6 (and_6_out, in_9, not_15_out);
  not not_15 (not_15_out, in_8);
  not not_16 (not_16_out, in_9);
  and and_7 (and_7_out, not_16_out, in_8);
  and and_8 (and_8_out, in_9, in_8);
  not not_17 (not_17_out, in_5);
  and and_9 (and_9_out, not_17_out, not_18_out);
  not not_18 (not_18_out, in_4);
  not not_19 (not_19_out, in_3);
  and and_10 (and_10_out, in_5, not_20_out);
  not not_20 (not_20_out, in_4);
  not not_21 (not_21_out, in_3);
  not not_22 (not_22_out, in_5);
  and and_11 (and_11_out, not_22_out, in_4);
  not not_23 (not_23_out, in_3);
  and and_12 (and_12_out, in_5, in_4);
  not not_24 (not_24_out, in_3);
  and and_13 (and_13_out, not_1_out, not_2_out);
  and and_14 (and_14_out, in_5, not_3_out);
  and and_15 (and_15_out, not_4_out, in_4);
  and and_16 (and_16_out, in_5, in_4);
  and and_17 (and_17_out, and_1_out, not_7_out);
  not not_25 (not_25_out, in_6);
  and and_18 (and_18_out, and_2_out, not_9_out);
  not not_26 (not_26_out, in_6);
  and and_19 (and_19_out, and_3_out, not_11_out);
  not not_27 (not_27_out, in_6);
  and and_20 (and_20_out, and_4_out, not_12_out);
  not not_28 (not_28_out, in_6);
  and and_21 (and_21_out, and_5_out, BULAN);
  not not_29 (not_29_out, in_6);
  and and_22 (and_22_out, and_6_out, BULAN);
  not not_30 (not_30_out, in_6);
  and and_23 (and_23_out, and_7_out, BULAN);
  not not_31 (not_31_out, in_6);
  and and_24 (and_24_out, and_8_out, BULAN);
  not not_32 (not_32_out, in_6);
  and and_25 (and_25_out, and_9_out, not_19_out);
  and and_26 (and_26_out, and_25_out, not_33_out);
  not not_33 (not_33_out, TANGGAL);
  not not_34 (not_34_out, in_1);
  and and_27 (and_27_out, and_10_out, not_21_out);
  and and_28 (and_28_out, and_27_out, not_35_out);
  not not_35 (not_35_out, TANGGAL);
  not not_36 (not_36_out, in_1);
  and and_29 (and_29_out, and_11_out, not_23_out);
  and and_30 (and_30_out, and_29_out, not_37_out);
  not not_37 (not_37_out, TANGGAL);
  not not_38 (not_38_out, in_1);
  and and_31 (and_31_out, and_12_out, not_24_out);
  and and_32 (and_32_out, and_31_out, not_39_out);
  not not_39 (not_39_out, TANGGAL);
  not not_40 (not_40_out, in_1);
  and and_33 (and_33_out, and_13_out, in_3);
  and and_34 (and_34_out, and_33_out, not_41_out);
  not not_41 (not_41_out, TANGGAL);
  not not_42 (not_42_out, in_1);
  and and_35 (and_35_out, and_14_out, in_3);
  and and_36 (and_36_out, and_35_out, not_43_out);
  not not_43 (not_43_out, TANGGAL);
  not not_44 (not_44_out, in_1);
  and and_37 (and_37_out, and_15_out, in_3);
  and and_38 (and_38_out, and_37_out, not_45_out);
  not not_45 (not_45_out, TANGGAL);
  not not_46 (not_46_out, in_1);
  and and_39 (and_39_out, and_16_out, in_3);
  and and_40 (and_40_out, and_39_out, not_47_out);
  not not_47 (not_47_out, TANGGAL);
  not not_48 (not_48_out, in_1);
  and and_41 (and_41_out, and_17_out, not_25_out);
  and and_42 (and_42_out, and_18_out, not_26_out);
  and and_43 (and_43_out, and_19_out, not_27_out);
  and and_44 (and_44_out, and_20_out, not_28_out);
  and and_45 (and_45_out, and_21_out, not_29_out);
  and and_46 (and_46_out, and_22_out, not_30_out);
  and and_47 (and_47_out, and_23_out, not_31_out);
  and and_48 (and_48_out, and_24_out, not_32_out);
  and and_49 (and_49_out, and_26_out, not_34_out);
  and and_50 (and_50_out, and_28_out, not_36_out);
  and and_51 (and_51_out, and_30_out, not_38_out);
  and and_52 (and_52_out, and_32_out, not_40_out);
  and and_53 (and_53_out, and_34_out, not_42_out);
  and and_54 (and_54_out, and_36_out, not_44_out);
  and and_55 (and_55_out, and_38_out, not_46_out);
  and and_56 (and_56_out, and_40_out, not_48_out);
  or or_1 (or_1_out, and_48_out, and_47_out);
  or or_2 (or_2_out, or_1_out, and_46_out);
  or or_3 (or_3_out, or_2_out, and_45_out);
  _7_Segment_Display u_7_segment_display_1 (
    .g(PG_out), .f(PF_out), .a(PA_out), .b(PB_out), .e(PE_out), .d(PD_out), .c(PC_out));  // open: dp
  not not_49 (not_49_out, in_9);
  not not_50 (not_50_out, in_8);
  not not_51 (not_51_out, in_8);
  not not_52 (not_52_out, in_9);
  or or_4 (or_4_out, or_3_out, and_44_out);
  or or_5 (or_5_out, or_4_out, and_43_out);
  or or_6 (or_6_out, or_5_out, and_42_out);
  or or_7 (or_7_out, or_6_out, and_41_out);
  _7_Segment_Display u_7_segment_display_2 (
    .g(G_out), .f(F_out), .a(A_out), .b(B_out), .e(E_out), .d(D_out), .c(C_out));  // open: dp
  and and_57 (and_57_out, not_49_out, not_50_out);
  and and_58 (and_58_out, and_57_out, not_53_out);
  not not_53 (not_53_out, BULAN);
  and and_59 (and_59_out, in_9, not_51_out);
  and and_60 (and_60_out, and_59_out, not_54_out);
  not not_54 (not_54_out, BULAN);
  and and_61 (and_61_out, not_52_out, in_8);
  and and_62 (and_62_out, and_61_out, not_55_out);
  not not_55 (not_55_out, BULAN);
  and and_63 (and_63_out, in_9, in_8);
  and and_64 (and_64_out, and_63_out, not_56_out);
  not not_56 (not_56_out, BULAN);
  or or_8 (or_8_out, or_7_out, and_73_out);
  or MS0 (MS0_out, or_8_out, and_74_out);
  _7_Segment_Display u_7_segment_display_3 (
    .g(1'b0), .f(MS0_out), .a(MS0_out), .b(or_9_out), .e(MS0_out), .d(MS0_out), .c(or_10_out));  // open: dp
  _7_Segment_Display u_7_segment_display_4 (
    .g(or_75_out), .f(or_74_out), .a(or_69_out), .b(or_70_out), .e(or_73_out), .d(or_72_out), .c(or_71_out));  // open: dp
  not not_57 (not_57_out, in_5);
  and and_65 (and_65_out, not_57_out, not_58_out);
  not not_58 (not_58_out, in_4);
  not not_59 (not_59_out, in_3);
  and and_66 (and_66_out, in_5, not_60_out);
  not not_60 (not_60_out, in_4);
  not not_61 (not_61_out, in_3);
  not not_62 (not_62_out, in_5);
  and and_67 (and_67_out, not_62_out, in_4);
  not not_63 (not_63_out, in_3);
  and and_68 (and_68_out, in_5, in_4);
  not not_64 (not_64_out, in_3);
  not not_65 (not_65_out, in_5);
  and and_69 (and_69_out, not_65_out, not_66_out);
  not not_66 (not_66_out, in_4);
  and and_70 (and_70_out, in_5, not_67_out);
  not not_67 (not_67_out, in_4);
  not not_68 (not_68_out, in_5);
  and and_71 (and_71_out, not_68_out, in_4);
  and and_72 (and_72_out, in_5, in_4);
  and and_73 (and_73_out, and_58_out, in_6);
  and and_74 (and_74_out, and_60_out, in_6);
  and and_75 (and_75_out, and_62_out, in_6);
  and and_76 (and_76_out, and_64_out, in_6);
  or or_9 (or_9_out, MS0_out, MS1_out);
  or or_10 (or_10_out, MS0_out, MS1_out);
  and and_77 (and_77_out, and_65_out, not_59_out);
  and and_78 (and_78_out, and_66_out, not_61_out);
  and and_79 (and_79_out, and_67_out, not_63_out);
  and and_80 (and_80_out, and_68_out, not_64_out);
  and and_81 (and_81_out, and_69_out, in_3);
  and and_82 (and_82_out, and_70_out, in_3);
  and and_83 (and_83_out, and_71_out, in_3);
  and and_84 (and_84_out, and_72_out, in_3);
  or or_11 (or_11_out, and_41_out, and_75_out);
  or MS1 (MS1_out, and_75_out, and_76_out);
  and and_85 (and_85_out, and_77_out, TANGGAL);
  and and_86 (and_86_out, and_85_out, not_69_out);
  not not_69 (not_69_out, in_1);
  and and_87 (and_87_out, and_78_out, TANGGAL);
  and and_88 (and_88_out, and_87_out, not_70_out);
  not not_70 (not_70_out, in_1);
  and and_89 (and_89_out, and_79_out, TANGGAL);
  and and_90 (and_90_out, and_89_out, not_71_out);
  not not_71 (not_71_out, in_1);
  and and_91 (and_91_out, and_80_out, TANGGAL);
  and and_92 (and_92_out, and_91_out, not_72_out);
  not not_72 (not_72_out, in_1);
  and and_93 (and_93_out, and_81_out, TANGGAL);
  and and_94 (and_94_out, and_93_out, not_73_out);
  not not_73 (not_73_out, in_1);
  and and_95 (and_95_out, and_82_out, TANGGAL);
  and and_96 (and_96_out, and_95_out, not_74_out);
  not not_74 (not_74_out, in_1);
  and and_97 (and_97_out, and_83_out, TANGGAL);
  and and_98 (and_98_out, and_97_out, not_75_out);
  not not_75 (not_75_out, in_1);
  and and_99 (and_99_out, and_84_out, TANGGAL);
  and and_100 (and_100_out, and_99_out, not_76_out);
  not not_76 (not_76_out, in_1);
  or or_12 (or_12_out, and_42_out, and_76_out);
  or or_13 (or_13_out, and_88_out, and_86_out);
  or or_14 (or_14_out, or_13_out, and_56_out);
  or or_15 (or_15_out, or_14_out, and_55_out);
  not not_77 (not_77_out, in_5);
  not not_78 (not_78_out, in_4);
  not not_79 (not_79_out, in_4);
  not not_80 (not_80_out, in_5);
  not not_81 (not_81_out, in_5);
  not not_82 (not_82_out, in_4);
  not not_83 (not_83_out, in_4);
  not not_84 (not_84_out, in_5);
  or or_16 (or_16_out, or_15_out, and_54_out);
  or or_17 (or_17_out, or_16_out, and_53_out);
  or or_18 (or_18_out, or_17_out, and_52_out);
  or or_19 (or_19_out, or_18_out, and_51_out);
  and and_101 (and_101_out, not_77_out, not_78_out);
  and and_102 (and_102_out, and_101_out, not_85_out);
  not not_85 (not_85_out, in_3);
  not not_86 (not_86_out, TANGGAL);
  and and_103 (and_103_out, in_5, not_79_out);
  and and_104 (and_104_out, and_103_out, not_87_out);
  not not_87 (not_87_out, in_3);
  not not_88 (not_88_out, TANGGAL);
  and and_105 (and_105_out, not_80_out, in_4);
  and and_106 (and_106_out, and_105_out, not_89_out);
  not not_89 (not_89_out, in_3);
  not not_90 (not_90_out, TANGGAL);
  and and_107 (and_107_out, in_5, in_4);
  and and_108 (and_108_out, and_107_out, not_91_out);
  not not_91 (not_91_out, in_3);
  not not_92 (not_92_out, TANGGAL);
  and and_109 (and_109_out, not_81_out, not_82_out);
  and and_110 (and_110_out, and_109_out, in_3);
  not not_93 (not_93_out, TANGGAL);
  and and_111 (and_111_out, in_5, not_83_out);
  and and_112 (and_112_out, and_111_out, in_3);
  not not_94 (not_94_out, TANGGAL);
  and and_113 (and_113_out, not_84_out, in_4);
  and and_114 (and_114_out, and_113_out, in_3);
  not not_95 (not_95_out, TANGGAL);
  and and_115 (and_115_out, in_5, in_4);
  and and_116 (and_116_out, and_115_out, in_3);
  not not_96 (not_96_out, TANGGAL);
  or or_20 (or_20_out, or_19_out, and_50_out);
  or P0 (P0_out, or_20_out, and_49_out);
  and and_117 (and_117_out, and_102_out, not_86_out);
  and and_118 (and_118_out, and_104_out, not_88_out);
  and and_119 (and_119_out, and_106_out, not_90_out);
  and and_120 (and_120_out, and_108_out, not_92_out);
  and and_121 (and_121_out, and_110_out, not_93_out);
  and and_122 (and_122_out, and_112_out, not_94_out);
  and and_123 (and_123_out, and_114_out, not_95_out);
  and and_124 (and_124_out, and_116_out, not_96_out);
  and and_125 (and_125_out, and_117_out, in_1);
  and and_126 (and_126_out, and_118_out, in_1);
  and and_127 (and_127_out, and_119_out, in_1);
  and and_128 (and_128_out, and_120_out, in_1);
  and and_129 (and_129_out, and_121_out, in_1);
  and and_130 (and_130_out, and_122_out, in_1);
  and and_131 (and_131_out, and_123_out, in_1);
  and and_132 (and_132_out, and_124_out, in_1);
  or or_21 (or_21_out, P0_out, P1_out);
  or or_22 (or_22_out, P0_out, P2_out);
  or PA (PA_out, or_22_out, P3_out);
  or or_23 (or_23_out, or_21_out, P2_out);
  or PB (PB_out, or_23_out, P3_out);
  or or_24 (or_24_out, P0_out, P1_out);
  or PC (PC_out, or_24_out, P3_out);
  or or_25 (or_25_out, P0_out, P2_out);
  or PD (PD_out, or_25_out, P3_out);
  or PE (PE_out, P0_out, P2_out);
  or PF (PF_out, P0_out, P0_out);
  or PG (PG_out, P2_out, P3_out);
  or or_26 (or_26_out, or_12_out, or_11_out);
  or or_27 (or_27_out, and_128_out, and_127_out);
  or or_28 (or_28_out, or_27_out, and_126_out);
  or or_29 (or_29_out, or_28_out, and_125_out);
  or or_30 (or_30_out, and_43_out, or_11_out);
  or or_31 (or_31_out, or_12_out, or_11_out);
  or or_32 (or_32_out, and_44_out, or_26_out);
  not not_97 (not_97_out, in_5);
  not not_98 (not_98_out, in_4);
  not not_99 (not_99_out, in_4);
  not not_100 (not_100_out, in_5);
  not not_101 (not_101_out, in_5);
  not not_102 (not_102_out, in_4);
  not not_103 (not_103_out, in_4);
  not not_104 (not_104_out, in_5);
  or or_33 (or_33_out, or_29_out, and_100_out);
  or or_34 (or_34_out, or_33_out, and_98_out);
  or or_35 (or_35_out, or_34_out, and_96_out);
  or or_36 (or_36_out, or_35_out, and_94_out);
  or or_37 (or_37_out, and_46_out, or_38_out);
  or or_38 (or_38_out, and_44_out, or_30_out);
  or or_39 (or_39_out, and_44_out, or_40_out);
  or or_40 (or_40_out, and_43_out, or_31_out);
  or or_41 (or_41_out, and_46_out, or_42_out);
  or or_42 (or_42_out, and_45_out, or_32_out);
  or or_43 (or_43_out, and_44_out, or_44_out);
  or or_44 (or_44_out, and_43_out, or_11_out);
  or or_45 (or_45_out, and_45_out, or_11_out);
  or or_46 (or_46_out, and_45_out, or_47_out);
  or or_47 (or_47_out, and_44_out, and_43_out);
  and and_133 (and_133_out, not_97_out, not_98_out);
  not not_105 (not_105_out, in_3);
  and and_134 (and_134_out, in_5, not_99_out);
  not not_106 (not_106_out, in_3);
  and and_135 (and_135_out, not_100_out, in_4);
  not not_107 (not_107_out, in_3);
  and and_136 (and_136_out, in_5, in_4);
  not not_108 (not_108_out, in_3);
  and and_137 (and_137_out, not_101_out, not_102_out);
  and and_138 (and_138_out, in_5, not_103_out);
  and and_139 (and_139_out, not_104_out, in_4);
  and and_140 (and_140_out, in_5, in_4);
  or or_48 (or_48_out, or_36_out, and_92_out);
  or P1 (P1_out, or_48_out, and_90_out);
  or or_49 (or_49_out, and_47_out, or_37_out);
  or or_50 (or_50_out, and_45_out, or_39_out);
  or or_51 (or_51_out, and_47_out, or_41_out);
  or or_52 (or_52_out, and_46_out, or_43_out);
  or or_53 (or_53_out, and_46_out, or_45_out);
  or or_54 (or_54_out, and_46_out, or_46_out);
  and and_141 (and_141_out, and_133_out, not_105_out);
  and and_142 (and_142_out, and_141_out, TANGGAL);
  and and_143 (and_143_out, and_134_out, not_106_out);
  and and_144 (and_144_out, and_143_out, TANGGAL);
  and and_145 (and_145_out, and_135_out, not_107_out);
  and and_146 (and_146_out, and_145_out, TANGGAL);
  and and_147 (and_147_out, and_136_out, not_108_out);
  and and_148 (and_148_out, and_147_out, TANGGAL);
  and and_149 (and_149_out, and_137_out, in_3);
  and and_150 (and_150_out, and_149_out, TANGGAL);
  and and_151 (and_151_out, and_138_out, in_3);
  and and_152 (and_152_out, and_151_out, TANGGAL);
  and and_153 (and_153_out, and_139_out, in_3);
  and and_154 (and_154_out, and_153_out, TANGGAL);
  and and_155 (and_155_out, and_140_out, in_3);
  and and_156 (and_156_out, and_155_out, TANGGAL);
  or or_55 (or_55_out, and_73_out, or_56_out);
  or or_56 (or_56_out, and_48_out, or_49_out);
  or or_57 (or_57_out, and_73_out, or_58_out);
  or or_58 (or_58_out, and_48_out, or_50_out);
  or or_59 (or_59_out, and_73_out, or_60_out);
  or or_60 (or_60_out, and_48_out, or_51_out);
  or or_61 (or_61_out, and_73_out, or_62_out);
  or or_62 (or_62_out, and_47_out, or_52_out);
  or or_63 (or_63_out, and_47_out, or_64_out);
  or or_64 (or_64_out, and_43_out, or_11_out);
  or or_65 (or_65_out, and_73_out, or_66_out);
  or or_66 (or_66_out, and_47_out, or_53_out);
  or or_67 (or_67_out, and_73_out, or_68_out);
  or or_68 (or_68_out, and_47_out, or_54_out);
  and and_157 (and_157_out, and_142_out, in_1);
  and and_158 (and_158_out, and_144_out, in_1);
  and and_159 (and_159_out, and_146_out, in_1);
  and and_160 (and_160_out, and_148_out, in_1);
  and and_161 (and_161_out, and_150_out, in_1);
  and and_162 (and_162_out, and_152_out, in_1);
  and and_163 (and_163_out, and_154_out, in_1);
  and and_164 (and_164_out, and_156_out, in_1);
  or or_69 (or_69_out, and_74_out, or_55_out);
  or or_70 (or_70_out, and_74_out, or_57_out);
  or or_71 (or_71_out, and_74_out, or_59_out);
  or or_72 (or_72_out, and_74_out, or_61_out);
  or or_73 (or_73_out, and_73_out, or_63_out);
  or or_74 (or_74_out, and_74_out, or_65_out);
  or or_75 (or_75_out, and_74_out, or_67_out);
  or or_76 (or_76_out, and_49_out, and_90_out);
  or or_77 (or_77_out, and_129_out, and_130_out);
  or or_78 (or_78_out, or_77_out, and_131_out);
  or or_79 (or_79_out, or_78_out, and_132_out);
  or or_80 (or_80_out, or_79_out, and_157_out);
  or M0 (M0_out, or_81_out, and_163_out);
  or or_81 (or_81_out, or_76_out, and_129_out);
  or or_82 (or_82_out, or_80_out, and_158_out);
  or or_83 (or_83_out, or_82_out, and_159_out);
  or or_84 (or_84_out, or_83_out, and_160_out);
  or or_85 (or_85_out, or_84_out, and_161_out);
  or or_86 (or_86_out, or_87_out, and_130_out);
  or or_87 (or_87_out, and_50_out, and_92_out);
  or P2 (P2_out, or_85_out, and_162_out);
  or M1 (M1_out, or_86_out, and_164_out);
  or P3 (P3_out, and_164_out, and_163_out);
  or or_88 (or_88_out, M2_out, M0_out);
  or or_89 (or_89_out, M1_out, M0_out);
  or or_90 (or_90_out, M3_out, or_91_out);
  or or_91 (or_91_out, M1_out, M0_out);
  or M2 (M2_out, or_92_out, and_131_out);
  or or_92 (or_92_out, and_51_out, and_94_out);
  or or_93 (or_93_out, M3_out, or_88_out);
  or or_94 (or_94_out, M2_out, or_89_out);
  or or_95 (or_95_out, M4_out, or_90_out);
  or or_96 (or_96_out, M2_out, M0_out);
  or or_97 (or_97_out, M3_out, M2_out);
  or or_98 (or_98_out, M6_out, or_99_out);
  or or_99 (or_99_out, M5_out, or_93_out);
  or or_100 (or_100_out, M4_out, or_101_out);
  or or_101 (or_101_out, M3_out, or_94_out);
  or or_102 (or_102_out, M6_out, or_103_out);
  or or_103 (or_103_out, M5_out, or_95_out);
  or or_104 (or_104_out, M5_out, or_105_out);
  or or_105 (or_105_out, M3_out, or_96_out);
  or or_106 (or_106_out, M5_out, or_107_out);
  or or_107 (or_107_out, M4_out, M0_out);
  or or_108 (or_108_out, M5_out, or_109_out);
  or or_109 (or_109_out, M4_out, or_97_out);
  or M3 (M3_out, or_110_out, and_132_out);
  or or_110 (or_110_out, and_52_out, and_96_out);
  or or_111 (or_111_out, M8_out, or_112_out);
  or or_112 (or_112_out, M7_out, or_98_out);
  or or_113 (or_113_out, M8_out, or_114_out);
  or or_114 (or_114_out, M7_out, or_100_out);
  or or_115 (or_115_out, M8_out, or_116_out);
  or or_116 (or_116_out, M7_out, or_102_out);
  or or_117 (or_117_out, M8_out, or_118_out);
  or or_118 (or_118_out, M6_out, or_104_out);
  or or_119 (or_119_out, M2_out, M0_out);
  or or_120 (or_120_out, M6_out, or_106_out);
  or or_121 (or_121_out, M6_out, or_108_out);
  or A (A_out, M9_out, or_111_out);
  or B (B_out, M9_out, or_113_out);
  or C (C_out, M9_out, or_115_out);
  or D (D_out, M9_out, or_117_out);
  or E (E_out, M8_out, or_122_out);
  or or_122 (or_122_out, M6_out, or_119_out);
  or F (F_out, M9_out, or_123_out);
  or or_123 (or_123_out, M8_out, or_120_out);
  or G (G_out, M9_out, or_124_out);
  or or_124 (or_124_out, M8_out, or_121_out);
  or M4 (M4_out, or_125_out, and_157_out);
  or or_125 (or_125_out, and_53_out, and_98_out);
  or M5 (M5_out, or_126_out, and_158_out);
  or or_126 (or_126_out, and_54_out, and_100_out);
  or M6 (M6_out, or_127_out, and_159_out);
  or or_127 (or_127_out, and_55_out, and_125_out);
  or M7 (M7_out, or_128_out, and_160_out);
  or or_128 (or_128_out, and_56_out, and_126_out);
  or M8 (M8_out, or_129_out, and_161_out);
  or or_129 (or_129_out, and_86_out, and_127_out);
  or or_130 (or_130_out, and_88_out, and_128_out);
  or M9 (M9_out, or_130_out, and_162_out);
endmodule
